// Logisim project mips-cpu.circ as structural Verilog: 10 circuits, main circuit main
module main (
  input  in_1
);

  wire ALUSrc, clk, IfBeq, IfZero, Mem2Reg, MemWrite, RegDst, RegWrite;
  wire [1:0] ALUOp, ExtOp;
  wire [4:0] multiplexer_1_out, rs, rt;
  wire [5:0] func, OpCode;
  wire [15:6] immed;
  wire [31:0] alu_1_o, extender_1_out32, multiplexer_2_out, multiplexer_3_out, ram_1_data, regfile_1_rd1,
       regfile_1_rd2;

  Clock clock_1 (.out(clk));
  IFU ifu_1 (.IfBeq(IfBeq), .Instr({OpCode, rs, rt, immed, func}), .clk(clk), .reset(in_1), .IfZero(IfZero));
  Controller controller_1 (
    .OpCode(OpCode), .Func(func), .RegDst(RegDst), .ALUSrc(ALUSrc), .Mem2Reg(Mem2Reg), .RegWrite(RegWrite),
    .MemWrite(MemWrite), .IfBeq(IfBeq), .ExtOp(ExtOp), .ALUOp(ALUOp));
  Multiplexer #(.width(5)) multiplexer_1 (
    .in0(rt), .in1(immed[15:11]), .out(multiplexer_1_out), .sel(RegDst));  // open: en
  RegFile regfile_1 (
    .clk(clk), .A3(multiplexer_1_out), .RegWrite(RegWrite), .RD1(regfile_1_rd1), .A1(rs), .A2(rt),
    .RD2(regfile_1_rd2), .WD(multiplexer_2_out));
  Multiplexer #(.width(32), .disabled(0)) multiplexer_2 (
    .in0(alu_1_o), .in1(ram_1_data), .out(multiplexer_2_out), .sel(Mem2Reg));  // open: en
  Extender extender_1 (.In16({immed, func}), .ExtOp(ExtOp), .Out32(extender_1_out32));
  Multiplexer #(.width(32)) multiplexer_3 (
    .in0(regfile_1_rd2), .in1(extender_1_out32), .out(multiplexer_3_out), .sel(ALUSrc));  // open: en
  ALU alu_1 (.A(regfile_1_rd1), .B(multiplexer_3_out), .O(alu_1_o), .ALUOp(ALUOp), .IfZero(IfZero));
  RAM #(.addrWidth(5), .dataWidth(32), .bus("separate")) ram_1 (
    .addr(alu_1_o[4:0]), .din(regfile_1_rd2), .data(ram_1_data), .str(MemWrite), .clk(clk), .clr(in_1));  // open: sel, ld

  // Other names for the same wires on the sheet: immed[5:0] = func; rd[4:0] = immed[15:11]; reset = in_1;
  //   shamt[4:0] = immed[10:6]

  // Notes on the sheet:
  //   DM
endmodule

module Controller (
  input  [5:0] OpCode,
  input  [5:0] Func,
  output RegDst,
  output ALUSrc,
  output Mem2Reg,
  output RegWrite,
  output MemWrite,
  output IfBeq,
  output [1:0] ExtOp,
  output [1:0] ALUOp
);

  wire addu_out, beq_out, lui_out, lw_out, not_1_out, not_2_out, not_3_out, not_4_out, not_5_out, not_6_out,
       not_11_out, not_12_out, ori_out, subu_out, sw_out;

  not not_1 (not_1_out, OpCode[5]);
  not not_2 (not_2_out, OpCode[3]);
  not not_3 (not_3_out, OpCode[4]);
  not not_4 (not_4_out, OpCode[2]);
  not not_5 (not_5_out, OpCode[0]);
  not not_6 (not_6_out, OpCode[1]);
  // NOT_Gate not_7 has open pins: in=Func[5], out=open
  // NOT_Gate not_8 has open pins: in=Func[3], out=open
  // NOT_Gate not_9 has open pins: in=Func[4], out=open
  // NOT_Gate not_10 has open pins: in=Func[2], out=open
  not not_11 (not_11_out, Func[1]);
  not not_12 (not_12_out, Func[0]);
  and addu (addu_out, not_4_out, not_6_out, not_11_out, Func[0]);
  and subu (subu_out, not_4_out, not_6_out, Func[1], Func[0]);
  and ori (ori_out, not_6_out, OpCode[0]);
  and lw (lw_out, OpCode[5], not_2_out);
  and sw (sw_out, OpCode[5], OpCode[3]);
  and beq (beq_out, OpCode[2], not_5_out);
  and lui (lui_out, OpCode[2], OpCode[1]);
  or u_ALUSrc (ALUSrc, ori_out, lw_out, sw_out, lui_out);
  or u_RegDst (RegDst, addu_out, subu_out);
  buf u_Mem2Reg (Mem2Reg, lw_out);  // OR_Gate
  or u_RegWrite (RegWrite, addu_out, subu_out, ori_out, lw_out, lui_out);
  buf u_MemWrite (MemWrite, sw_out);  // OR_Gate
  buf u_IfBeq (IfBeq, beq_out);  // OR_Gate
  buf ExtOp_1 (ExtOp[1], lui_out);  // OR_Gate
  or ExtOp_0 (ExtOp[0], lw_out, sw_out);
  or ALUOp_0 (ALUOp[0], subu_out, beq_out);
  buf ALUOp_1 (ALUOp[1], ori_out);  // OR_Gate

  // Notes on the sheet:
  //   addu
  //   subu
  //   ori
  //   lw
  //   sw
  //   beq
  //   lui
  //   Op
  //   000000
  //   000000
  //   001101
  //   100011
  //   101011
  //   000100
  //   001111
  //   func
  //   100001
  //   100011
endmodule

module IFU (
  input  IfBeq,
  input  IfZero,
  input  clk,
  input  reset,
  output [31:0] Instr
);

  wire and_1_out;
  wire [29:0] multiplexer_1_out, PC_q;
  wire [31:0] bit_extender_1_out, bit_extender_2_out, n32adder_1_s, n32adder_2_s;
  wire [31:30] multiplexer_1_out_2;

  Register #(.width(30)) PC (.D(multiplexer_1_out), .Q(PC_q), .clk(clk), .clr(reset));  // open: en
  assign bit_extender_1_out = {{2{1'b0}}, PC_q};  // Bit_Extender bit_extender_1
  _32Adder u_32adder_1 (.S(n32adder_1_s), .A(bit_extender_1_out), .B(32'h1));
  ROM #(.addrWidth(5), .dataWidth(32)) rom_1 (.addr(PC_q[4:0]), .data(Instr));  // open: sel
  assign bit_extender_2_out = {{16{1'b0}}, Instr[15:0]};  // Bit_Extender bit_extender_2
  _32Adder u_32adder_2 (.S(n32adder_2_s), .A(n32adder_1_s), .B(bit_extender_2_out));
  Multiplexer #(.width(32)) multiplexer_1 (
    .in0(n32adder_1_s), .in1(n32adder_2_s), .out({multiplexer_1_out_2, multiplexer_1_out}), .sel(and_1_out));  // open: en
  and and_1 (and_1_out, IfBeq, IfZero);

  // Notes on the sheet:
  //   字地址，所以+1
  //   contents of rom_1 (hex, n*v repeats v):
  //   3c080001 3c090001 3c0a0001 35080064 35290001 10a4023 12a4823 3c0a0000 3c0b0000 3c0c0000 1485021
  //   1886021 1094023 1485021 1685821 1094023 11000001 1000fff8 ac0a0000 ac0b0001 ac0c0002 8c0d0000
  //   8c0e0001 8c0f0002
endmodule

// 寄存器堆
module RegFile (
  input  clk,
  input  [31:0] WD,
  input  [4:0] A3,
  input  RegWrite,
  input  [4:0] A1,
  input  [4:0] A2,
  output [31:0] RD1,
  output [31:0] RD2
);

  wire decoder_1_out0, decoder_1_out1, decoder_1_out2, decoder_1_out3, decoder_1_out4, decoder_1_out5,
       decoder_1_out6, decoder_1_out7, decoder_1_out8, decoder_1_out9, decoder_1_out10, decoder_1_out11,
       decoder_1_out12, decoder_1_out13, decoder_1_out14, decoder_1_out15, decoder_1_out16, decoder_1_out17,
       decoder_1_out18, decoder_1_out19, decoder_1_out20, decoder_1_out21, decoder_1_out22, decoder_1_out23,
       decoder_1_out24, decoder_1_out25, decoder_1_out26, decoder_1_out27, decoder_1_out28, decoder_1_out29,
       decoder_1_out30, decoder_1_out31;
  wire [31:0] _0, _1, _2, _3, _4, _5, _6, _7, _8, _9, _10, _11, _12, _13, _14, _15, _16, _17, _18, _19, _20,
       _21, _22, _23, _24, _25, _26, _27, _28, _29, _30, _31;

  Decoder #(.select(5), .disabled(0)) decoder_1 (
    .out0(decoder_1_out0), .out1(decoder_1_out1), .out2(decoder_1_out2), .out3(decoder_1_out3),
    .out4(decoder_1_out4), .out5(decoder_1_out5), .out6(decoder_1_out6), .out7(decoder_1_out7),
    .out8(decoder_1_out8), .out9(decoder_1_out9), .out10(decoder_1_out10), .out11(decoder_1_out11),
    .out12(decoder_1_out12), .out13(decoder_1_out13), .out14(decoder_1_out14), .out15(decoder_1_out15),
    .out16(decoder_1_out16), .out17(decoder_1_out17), .out18(decoder_1_out18), .out19(decoder_1_out19),
    .out20(decoder_1_out20), .out21(decoder_1_out21), .out22(decoder_1_out22), .out23(decoder_1_out23),
    .out24(decoder_1_out24), .out25(decoder_1_out25), .out26(decoder_1_out26), .out27(decoder_1_out27),
    .out28(decoder_1_out28), .out29(decoder_1_out29), .out30(decoder_1_out30), .out31(decoder_1_out31),
    .sel(A3), .en(RegWrite));
  Register #(.width(32)) register_1 (.en(decoder_1_out0), .Q(_0), .clk(clk));  // open: D, clr
  Register #(.width(32)) register_2 (.D(WD), .en(decoder_1_out1), .Q(_1), .clk(clk));  // open: clr
  Register #(.width(32)) register_3 (.D(WD), .en(decoder_1_out2), .Q(_2), .clk(clk));  // open: clr
  Register #(.width(32)) register_4 (.D(WD), .en(decoder_1_out3), .Q(_3), .clk(clk));  // open: clr
  Register #(.width(32)) register_5 (.D(WD), .en(decoder_1_out4), .Q(_4), .clk(clk));  // open: clr
  Register #(.width(32)) register_6 (.D(WD), .en(decoder_1_out5), .Q(_5), .clk(clk));  // open: clr
  Register #(.width(32)) register_7 (.D(WD), .en(decoder_1_out6), .Q(_6), .clk(clk));  // open: clr
  Register #(.width(32)) register_8 (.D(WD), .en(decoder_1_out7), .Q(_7), .clk(clk));  // open: clr
  Register #(.width(32)) register_9 (.D(WD), .en(decoder_1_out8), .Q(_8), .clk(clk));  // open: clr
  Register #(.width(32)) register_10 (.D(WD), .en(decoder_1_out9), .Q(_9), .clk(clk));  // open: clr
  Register #(.width(32)) register_11 (.D(WD), .en(decoder_1_out10), .Q(_10), .clk(clk));  // open: clr
  Register #(.width(32)) register_12 (.D(WD), .en(decoder_1_out11), .Q(_11), .clk(clk));  // open: clr
  Register #(.width(32)) register_13 (.D(WD), .en(decoder_1_out12), .Q(_12), .clk(clk));  // open: clr
  Register #(.width(32)) register_14 (.D(WD), .en(decoder_1_out13), .Q(_13), .clk(clk));  // open: clr
  Register #(.width(32)) register_15 (.D(WD), .en(decoder_1_out14), .Q(_14), .clk(clk));  // open: clr
  Register #(.width(32)) register_16 (.D(WD), .en(decoder_1_out15), .Q(_15), .clk(clk));  // open: clr
  Register #(.width(32)) register_17 (.D(WD), .en(decoder_1_out16), .Q(_16), .clk(clk));  // open: clr
  Register #(.width(32)) register_18 (.D(WD), .en(decoder_1_out17), .Q(_17), .clk(clk));  // open: clr
  Register #(.width(32)) register_19 (.D(WD), .en(decoder_1_out18), .Q(_18), .clk(clk));  // open: clr
  Register #(.width(32)) register_20 (.D(WD), .en(decoder_1_out19), .Q(_19), .clk(clk));  // open: clr
  Register #(.width(32)) register_21 (.D(WD), .en(decoder_1_out20), .Q(_20), .clk(clk));  // open: clr
  Register #(.width(32)) register_22 (.D(WD), .en(decoder_1_out21), .Q(_21), .clk(clk));  // open: clr
  Register #(.width(32)) register_23 (.D(WD), .en(decoder_1_out22), .Q(_22), .clk(clk));  // open: clr
  Register #(.width(32)) register_24 (.D(WD), .en(decoder_1_out23), .Q(_23), .clk(clk));  // open: clr
  Register #(.width(32)) register_25 (.D(WD), .en(decoder_1_out24), .Q(_24), .clk(clk));  // open: clr
  Register #(.width(32)) register_26 (.D(WD), .en(decoder_1_out25), .Q(_25), .clk(clk));  // open: clr
  Register #(.width(32)) register_27 (.D(WD), .en(decoder_1_out26), .Q(_26), .clk(clk));  // open: clr
  Register #(.width(32)) register_28 (.D(WD), .en(decoder_1_out27), .Q(_27), .clk(clk));  // open: clr
  Register #(.width(32)) register_29 (.D(WD), .en(decoder_1_out28), .Q(_28), .clk(clk));  // open: clr
  Register #(.width(32)) register_30 (.D(WD), .en(decoder_1_out29), .Q(_29), .clk(clk));  // open: clr
  Register #(.width(32)) register_31 (.D(WD), .en(decoder_1_out30), .Q(_30), .clk(clk));  // open: clr
  Register #(.width(32)) register_32 (.D(WD), .en(decoder_1_out31), .Q(_31), .clk(clk));  // open: clr
  Multiplexer #(.select(5), .width(32)) multiplexer_1 (
    .in0(_0), .in1(_1), .in2(_2), .in3(_3), .in4(_4), .in5(_5), .in6(_6), .in7(_7), .in8(_8), .in9(_9),
    .in10(_10), .in11(_11), .in12(_12), .in13(_13), .in14(_14), .in15(_15), .in16(_16), .in17(_17),
    .in18(_18), .in19(_19), .in20(_20), .in21(_21), .in22(_22), .in23(_23), .in24(_24), .in25(_25),
    .in26(_26), .in27(_27), .in28(_28), .in29(_29), .in30(_30), .in31(_31), .out(RD1), .sel(A1));  // open: en
  Multiplexer #(.select(5), .width(32)) multiplexer_2 (
    .in0(_0), .in1(_1), .in2(_2), .in3(_3), .in4(_4), .in5(_5), .in6(_6), .in7(_7), .in8(_8), .in9(_9),
    .in10(_10), .in11(_11), .in12(_12), .in13(_13), .in14(_14), .in15(_15), .in16(_16), .in17(_17),
    .in18(_18), .in19(_19), .in20(_20), .in21(_21), .in22(_22), .in23(_23), .in24(_24), .in25(_25),
    .in26(_26), .in27(_27), .in28(_28), .in29(_29), .in30(_30), .in31(_31), .out(RD2), .sel(A2));  // open: en
endmodule

module ALU (
  input  [31:0] A,
  input  [31:0] B,
  input  [1:0] ALUOp,
  output IfZero,
  output [31:0] O
);

  wire [31:0] n32adder_1_s, n32subtractor_1_res, or_1_out;

  _32Adder u_32adder_1 (.S(n32adder_1_s), .A(A), .B(B));
  _32Subtractor u_32subtractor_1 (.A(A), .B(B), .Res(n32subtractor_1_res));
  assign or_1_out = A | B;  // OR_Gate or_1, 32 bits wide
  Multiplexer #(.select(2), .width(32)) multiplexer_1 (
    .in0(n32adder_1_s), .in1(n32subtractor_1_res), .in2(or_1_out), .out(O), .sel(ALUOp));  // open: in3, en
  Comparator #(.width(32)) comparator_1 (.a({32{1'b0}}), .b(O), .eq(IfZero));  // open: gt, lt

  // Notes on the sheet:
  //   00 add
  //   01 sub
  //   10 or
endmodule

// EXT
module Extender (
  input  [15:0] In16,
  input  [1:0] ExtOp,
  output [31:0] Out32
);

  wire [31:0] bit_extender_1_out, bit_extender_2_out, shifter_1_out;

  assign bit_extender_1_out = {{16{1'b0}}, In16};  // Bit_Extender bit_extender_1
  assign bit_extender_2_out = {{16{In16[15]}}, In16};  // Bit_Extender bit_extender_2
  Shifter #(.width(32)) shifter_1 (.in(bit_extender_1_out), .\dist (5'b10000), .out(shifter_1_out));
  Multiplexer #(.select(2), .width(32)) multiplexer_1 (
    .in0(bit_extender_1_out), .in1(bit_extender_2_out), .in2(shifter_1_out), .out(Out32), .sel(ExtOp));  // open: in3, en

  // Notes on the sheet:
  //   左移16位
  //   00 zero-extend
  //   01 sign-extend
  //   10 lui,低16位补0
endmodule

module Half_Adder (
  input  A,
  input  B,
  output S,
  output C
);

  and and_1 (C, B, A);
  xor xor_1 (S, A, B);
endmodule

module Full_Adder (
  input  A,
  input  B,
  input  Cin,
  output S,
  output Cout
);

  wire and_1_out, and_2_out, and_3_out;

  and and_1 (and_1_out, A, B);
  and and_2 (and_2_out, B, Cin);
  and and_3 (and_3_out, A, Cin);
  or or_1 (Cout, and_1_out, and_3_out, and_2_out);
  xor xor_1 (S, A, B, Cin);
endmodule

module _32Adder (
  input  [31:0] A,
  input  [31:0] B,
  output [31:0] S
);

  wire full_adder_2_cout, full_adder_3_cout, full_adder_4_cout, full_adder_5_cout, full_adder_6_cout,
       full_adder_7_cout, full_adder_8_cout, full_adder_9_cout, full_adder_10_cout, full_adder_11_cout,
       full_adder_12_cout, full_adder_13_cout, full_adder_14_cout, full_adder_15_cout, full_adder_16_cout,
       full_adder_17_cout, full_adder_18_cout, full_adder_19_cout, full_adder_20_cout, full_adder_21_cout,
       full_adder_22_cout, full_adder_23_cout, full_adder_24_cout, full_adder_25_cout, full_adder_26_cout,
       full_adder_27_cout, full_adder_28_cout, full_adder_29_cout, full_adder_30_cout, full_adder_31_cout,
       half_adder_1_c;

  Full_Adder full_adder_1 (.A(B[31]), .B(A[31]), .Cin(full_adder_2_cout), .S(S[31]));  // open: Cout
  Full_Adder full_adder_2 (.A(B[30]), .B(A[30]), .Cin(full_adder_4_cout), .Cout(full_adder_2_cout), .S(S[30]));
  Full_Adder full_adder_3 (.A(B[28]), .B(A[28]), .Cin(full_adder_6_cout), .Cout(full_adder_3_cout), .S(S[28]));
  Full_Adder full_adder_4 (.A(B[29]), .B(A[29]), .Cin(full_adder_3_cout), .Cout(full_adder_4_cout), .S(S[29]));
  Full_Adder full_adder_5 (.A(B[26]), .B(A[26]), .Cin(full_adder_7_cout), .Cout(full_adder_5_cout), .S(S[26]));
  Full_Adder full_adder_6 (.A(B[27]), .B(A[27]), .Cin(full_adder_5_cout), .Cout(full_adder_6_cout), .S(S[27]));
  Full_Adder full_adder_7 (.A(B[25]), .B(A[25]), .Cin(full_adder_9_cout), .Cout(full_adder_7_cout), .S(S[25]));
  Full_Adder full_adder_8 (.A(B[23]), .B(A[23]), .Cin(full_adder_10_cout), .Cout(full_adder_8_cout), .S(S[23]));
  Full_Adder full_adder_9 (.A(B[24]), .B(A[24]), .Cin(full_adder_8_cout), .Cout(full_adder_9_cout), .S(S[24]));
  Full_Adder full_adder_10 (.A(B[22]), .B(A[22]), .Cin(full_adder_12_cout), .Cout(full_adder_10_cout), .S(S[22]));
  Full_Adder full_adder_11 (.A(B[20]), .B(A[20]), .Cin(full_adder_14_cout), .Cout(full_adder_11_cout), .S(S[20]));
  Full_Adder full_adder_12 (.A(B[21]), .B(A[21]), .Cin(full_adder_11_cout), .Cout(full_adder_12_cout), .S(S[21]));
  Full_Adder full_adder_13 (.A(B[18]), .B(A[18]), .Cin(full_adder_15_cout), .Cout(full_adder_13_cout), .S(S[18]));
  Full_Adder full_adder_14 (.A(B[19]), .B(A[19]), .Cin(full_adder_13_cout), .Cout(full_adder_14_cout), .S(S[19]));
  Full_Adder full_adder_15 (.A(B[17]), .B(A[17]), .Cin(full_adder_17_cout), .Cout(full_adder_15_cout), .S(S[17]));
  Full_Adder full_adder_16 (.A(B[15]), .B(A[15]), .Cin(full_adder_18_cout), .Cout(full_adder_16_cout), .S(S[15]));
  Full_Adder full_adder_17 (.A(B[16]), .B(A[16]), .Cin(full_adder_16_cout), .Cout(full_adder_17_cout), .S(S[16]));
  Full_Adder full_adder_18 (.A(B[14]), .B(A[14]), .Cin(full_adder_20_cout), .Cout(full_adder_18_cout), .S(S[14]));
  Full_Adder full_adder_19 (.A(B[12]), .B(A[12]), .Cin(full_adder_22_cout), .Cout(full_adder_19_cout), .S(S[12]));
  Full_Adder full_adder_20 (.A(B[13]), .B(A[13]), .Cin(full_adder_19_cout), .Cout(full_adder_20_cout), .S(S[13]));
  Full_Adder full_adder_21 (.A(B[10]), .B(A[10]), .Cin(full_adder_23_cout), .Cout(full_adder_21_cout), .S(S[10]));
  Full_Adder full_adder_22 (.A(B[11]), .B(A[11]), .Cin(full_adder_21_cout), .Cout(full_adder_22_cout), .S(S[11]));
  Full_Adder full_adder_23 (.A(B[9]), .B(A[9]), .Cin(full_adder_24_cout), .Cout(full_adder_23_cout), .S(S[9]));
  Full_Adder full_adder_24 (.A(B[8]), .B(A[8]), .Cin(full_adder_25_cout), .Cout(full_adder_24_cout), .S(S[8]));
  Full_Adder full_adder_25 (.A(B[7]), .B(A[7]), .Cin(full_adder_26_cout), .Cout(full_adder_25_cout), .S(S[7]));
  Full_Adder full_adder_26 (.A(B[6]), .B(A[6]), .Cin(full_adder_28_cout), .Cout(full_adder_26_cout), .S(S[6]));
  Full_Adder full_adder_27 (.A(B[4]), .B(A[4]), .Cin(full_adder_30_cout), .Cout(full_adder_27_cout), .S(S[4]));
  Full_Adder full_adder_28 (.A(B[5]), .B(A[5]), .Cin(full_adder_27_cout), .Cout(full_adder_28_cout), .S(S[5]));
  Full_Adder full_adder_29 (.A(B[2]), .B(A[2]), .Cin(full_adder_31_cout), .Cout(full_adder_29_cout), .S(S[2]));
  Full_Adder full_adder_30 (.A(B[3]), .B(A[3]), .Cin(full_adder_29_cout), .Cout(full_adder_30_cout), .S(S[3]));
  Full_Adder full_adder_31 (.A(B[1]), .B(A[1]), .Cin(half_adder_1_c), .Cout(full_adder_31_cout), .S(S[1]));
  Half_Adder half_adder_1 (.A(B[0]), .B(A[0]), .S(S[0]), .C(half_adder_1_c));
endmodule

module _32Subtractor (
  input  [31:0] A,
  input  [31:0] B,
  output [31:0] Res
);

  wire [31:0] n32adder_1_s, not_1_out;

  assign not_1_out = ~B;  // NOT_Gate not_1, 32 bits wide
  _32Adder u_32adder_1 (.S(n32adder_1_s), .A(not_1_out), .B(32'h1));
  _32Adder u_32adder_2 (.S(Res), .A(A), .B(n32adder_1_s));

  // Notes on the sheet:
  //   A - B
endmodule
